# Fritzing sketch hc_06_slave (saved by Fritzing 0.9.3b)
breadboards: 1

parts:
  Part1 = Arduino Uno (Rev3)
  MOTOR2 = 28BYJ-48 Stepper Motor
  X2 = X113647 Stepper Driver Board [part_number=X113647 package=board]
  R3 = Resistor [tolerance=±5% resistance=470 package=THT]
  R4 = Resistor [tolerance=±5% resistance=470 package=THT]
  LED3 = LED - 5mm [color="Red (633nm)" package="5 mm [THT]"]
  LED4 = LED - 5mm [color="Yellow (592nm)" package="5 mm [THT]"]
  Part2 = Bluetooth HC-05 Macho

nets:
  N1: Part1.D8, X2.IN4
  N2: Part1.D9_PWM, X2.IN3
  N3: Part1.D10_PWM/SS, X2.IN2
  N4: Part1.D11_PWM/MOSI, X2.IN1
  N5: Part1.D12/MISO, LED3.anode
  N6: Part1.D13/SCK, LED4.anode
  N7: Part1.D2, Part2.TXD
  N8: Part1.D3_PWM, Part2.RXD
  5V: Part1.5V, X2.+V, Part2.VCC
  GND: Part1.GND, X2.GND, R3.Pin_0, R4.Pin_0, Part2.GND
  N9: MOTOR2.BLUE, X2.BLUE
  N10: MOTOR2.PINK, X2.PINK
  N11: MOTOR2.RED, X2.RED
  N12: MOTOR2.ORANGE, X2.ORANGE
  N13: MOTOR2.YELLOW, X2.YELLOW
  N14: R3.Pin_1, LED4.cathode
  N15: R4.Pin_1, LED3.cathode

notes:
  HC-06 For Slave

custom parts:
  28BYJ-48 Stepper Motor: 28BYJ-48 gear-reduction stepper motor (small)
  X113647 Stepper Driver Board: A common stepper motor driver board based on ULN2003APG darlington array
