# Fritzing sketch robotik_2 (saved by Fritzing 0.9.3b)
breadboards: 1

parts:
  LED1 = LED - 5mm [color="Red (633nm)" package="5 mm [THT]"]
  LED2 = smd LED [color="Yellow (595nm)" package="0603 [SMD]"]
  S1 = Pushbutton [package="[THT]"]
  Part1 = Arduino Uno (Rev3) - ICSP
  R1 = Resistor [tolerance=±5% resistance=470 package=THT]
  R2 = Resistor [tolerance=±5% resistance=470 package=THT]

nets:
  N1: LED1.cathode, R1.Pin_0
  N2: LED1.anode, Part1.D12/MISO
  N3: LED2.cathode, R2.Pin_0
  N4: LED2.anode, Part1.ICSP_MOSI, Part1.D11_PWM/MOSI
  N5: S1.Pin_1, S1.Pin_2, Part1.GND, R1.Pin_1, R2.Pin_1
  N6: S1.Pin_3, S1.Pin_4, Part1.D2
