# Fritzing sketch potentiometer_buzzer (saved by Fritzing 0.9.3b)
breadboards: 1

parts:
  Part1 = Arduino Uno (Rev3)
  U2 = POT [package=pot_alpha_rv16af-20]
  J1 = Piezo Speaker

nets:
  N1: Part1.A0, U2.S
  N2: Part1.5V, U2.E
  N3: Part1.GND, U2.A, J1.pin1
