# Fritzing sketch hc_05_master (saved by Fritzing 0.9.3b)
breadboards: 1

parts:
  Part1 = Arduino Uno (Rev3)
  R3 = Resistor [tolerance=±5% resistance=470 package=THT]
  R4 = Resistor [tolerance=±5% resistance=470 package=THT]
  LED3 = LED - 5mm [color="Red (633nm)" package="5 mm [THT]"]
  LED4 = LED - 5mm [color="Yellow (592nm)" package="5 mm [THT]"]
  Part2 = Bluetooth HC-05 Macho

nets:
  N1: Part1.D12/MISO, LED3.anode
  N2: Part1.D13/SCK, LED4.anode
  N3: Part1.D2, Part2.TXD
  N4: Part1.D3_PWM, Part2.RXD
  5V: Part1.5V, Part2.VCC
  GND: Part1.GND, R3.Pin_0, R4.Pin_0, Part2.GND
  N5: R3.Pin_1, LED4.cathode
  N6: R4.Pin_1, LED3.cathode
