# Fritzing sketch park_sensoru (saved by Fritzing 0.9.3b)
circuit board: 8.46667cm x 5.64444cm
breadboards: 1

parts:
  Part1 = Arduino Uno (Rev3)
  J1 = Piezo Speaker
  hc-sr1 = hc-sr04
  R1 = Resistor [tolerance=±5% resistance=330 package="2512 [SMD]"]

nets:
  N1: Part1.D8, J1.pin2
  N2: Part1.D6_PWM, hc-sr1.Echo
  N3: Part1.D7, hc-sr1.Trig
  5V: Part1.5V, hc-sr1.VCC
  GND: Part1.GND, hc-sr1.GND, R1.Pin_1
  N4: J1.pin1, R1.Pin_0

// code stored in the sketch: Untitled.ino

