# Fritzing sketch lecture7 (saved by Fritzing 0.9.3b)
breadboards: 1

parts:
  Part1 = Arduino Uno (Rev3)
  DI1 = 7-Segment LED Display [package=THT]
  S1 = Pushbutton [package="[THT]"]
  R1 = Resistor [tolerance=±5% resistance=10k package="2512 [SMD]"]

nets:
  N1: Part1.D8, DI1.cathodeC
  N2: Part1.D9_PWM, DI1.cathodeD
  N3: Part1.D12/MISO, S1.Pin_3, S1.Pin_4
  N4: Part1.GND, S1.Pin_1, S1.Pin_2, R1.Pin_1
  N5: Part1.D2, DI1.cathodeA
  N6: Part1.D3_PWM, DI1.cathodeF
  N7: Part1.D4, DI1.cathodeE
  N8: Part1.D6_PWM, DI1.cathodeB
  N9: Part1.D7, DI1.cathodeG
  N10: DI1.commAnode, R1.Pin_0
